// Digital circuit LD15-MA-MB-AC-Logic.dig as structural Verilog
module LD15_MA_MB_AC_Logic (
  input  CLOCK_H,
  input  CLOCK_L,
  input  AND,
  input  TAD,
  input  DCA,
  input  JMS,
  input  ISZ,
  input  DEP,
  input  LDM,
  input  LDMA,
  input  LDMB,
  input  LDAC,
  input  CP0_H,
  input  CP1_H,
  input  CP2_H,
  input  CP3_H,
  input  CP0_L,
  input  OPG1_H,
  input  OPG2_H,
  input  A3,
  input  F0,
  input  F3,
  input  F5,
  input  F7,
  input  F8,
  input  F10,
  input  DEP_plus_EX__CP6,
  input  RDE,
  input  [11:0] IR,
  output WRITE,
  output AC_L,
  output MA_L,
  output MB_L,
  output OPG1_H_CP3_IR11
);

  wire nand_1_out, nand_2_out, nand_3_out, nand_5_out, nand_6_out, nand_7_out, nand_8_out, nand_9_out,
       nand_10_out, nand_11_out, nand_12_out, nand_13_out, nand_14_out, nand_16_out, nor_1_out, nor_2_out,
       not_1_out, not_2_out, not_3_out;

  not not_1 (not_1_out, LDMA);
  nand nand_1 (nand_1_out, DCA, JMS, LDM, ISZ, DEP);
  not not_2 (not_2_out, LDMB);
  nand nand_2 (nand_2_out, not_1_out, CP0_H);
  nand nand_3 (nand_3_out, nand_1_out, CP1_H);
  nor nor_1 (nor_1_out, nand_1_out, not_2_out);
  nand nand_4 (WRITE, nand_3_out, F7);
  nor nor_2 (nor_2_out, nor_1_out, CP0_L);
  not not_3 (not_3_out, nor_2_out);
  nand nand_5 (nand_5_out, not_3_out, F5, F7, F10);
  nand nand_6 (nand_6_out, nand_2_out, F0, A3, F3, F8, DEP_plus_EX__CP6);
  nand nand_7 (nand_7_out, CLOCK_L, MB_L);
  nand nand_8 (nand_8_out, CLOCK_L, MA_L);
  D_FF_AS d_ff_as_1 (.Set(~1'b1), .D(nand_5_out), .C(CLOCK_H), .Clr(~nand_7_out), .Q(MB_L));  // open: nQ
  D_FF_AS d_ff_as_2 (.Set(~1'b1), .D(nand_6_out), .C(CLOCK_H), .Clr(~nand_8_out), .Q(MA_L));  // open: nQ
  PullUp pullup_1 (.out(RDE));
  nand nand_9 (nand_9_out, AND, TAD, LDAC);
  nand nand_10 (nand_10_out, OPG1_H, IR[6]);
  nand nand_11 (nand_11_out, IR[9], OPG2_H);
  nand nand_12 (nand_12_out, nand_10_out, RDE, nand_11_out);
  nand nand_13 (nand_13_out, CP0_H, nand_9_out);
  nand nand_14 (nand_14_out, CP2_H, nand_12_out);
  nand nand_15 (OPG1_H_CP3_IR11, OPG1_H, IR[11], CP3_H);
  nand nand_16 (nand_16_out, nand_13_out, nand_14_out, OPG1_H_CP3_IR11);
  not not_4 (AC_L, nand_16_out);

  // Notes on the sheet:
  //   Support multiple devices using 
  //   RDE to load Data into AC by
  //   supporting Tri-State.
endmodule
