// Digital circuit TTY-Logic.dig as structural Verilog
module TTY_Logic (
  input  [11:0] IR,
  input  nCLRIN,
  input  IOP1_H,
  input  IOP2_H,
  input  IOP4_H,
  input  IOP1_L,
  input  TTY_IN_DATA_AVAILABLE,
  output PINT_PRINTER,
  output TTY_IN_CLOCK,
  output TTY_OUT_PRINT,
  output IOS_PRINTER,
  output PINT_KEYBOARD,
  output IOS_KEYBOARD,
  output RDA,
  output RDE
);

  wire and_1_out, and_2_out, and_3_out, and_4_out, and_5_out, d_ff_as_2_q, nor_1_out, not_1_out, not_2_out,
       not_3_out, or_1_out, or_2_out, TTY_IN, TTY_OUT;

  and and_1 (and_1_out, IOP4_H, TTY_OUT);
  and and_2 (and_2_out, IOP2_H, TTY_OUT);
  not not_1 (not_1_out, nCLRIN);
  and and_3 (and_3_out, IOP4_H, TTY_IN);
  not not_2 (not_2_out, nCLRIN);
  and and_4 (and_4_out, IOP4_H, TTY_IN);
  and and_5 (and_5_out, and_1_out, not_3_out);
  or or_1 (or_1_out, and_2_out, not_1_out);
  not not_3 (not_3_out, or_1_out);
  not not_4 (RDA, and_3_out);
  or or_2 (or_2_out, and_3_out, not_2_out);
  and and_6 (TTY_IN_CLOCK, TTY_IN_DATA_AVAILABLE, and_4_out);
  D_FF_AS d_ff_as_1 (.Set(and_5_out), .D(1'b1), .C(1'b0), .Clr(or_1_out), .Q(TTY_OUT_PRINT));  // open: nQ
  D_FF_AS d_ff_as_2 (.Set(1'b0), .D(1'b1), .C(TTY_IN_DATA_AVAILABLE), .Clr(or_2_out), .Q(d_ff_as_2_q));  // open: nQ
  Comparator #(.Bits(6)) x03x (.a(IR[8:3]), .b(6'b110000), .eq(TTY_IN));  // open: gt, lt
  Comparator #(.Bits(6)) x04x (.a(IR[8:3]), .b(6'b001000), .eq(TTY_OUT));  // open: gt, lt
  not not_5 (PINT_PRINTER, TTY_OUT_PRINT);
  nand nand_1 (IOS_PRINTER, TTY_OUT_PRINT, IOP1_H, TTY_OUT);
  nor nor_1 (nor_1_out, IOP1_L, IR[10]);
  nand nand_2 (IOS_KEYBOARD, d_ff_as_2_q, nor_1_out, TTY_IN);
  not not_6 (PINT_KEYBOARD, d_ff_as_2_q);
  not not_7 (RDE, and_4_out);
endmodule
